// Digital circuit multiplicacao8bits.dig as structural Verilog
module multiplicacao8bits (
  input  [7:0] A,
  input  [7:0] B
);

  wire Cout0, Cout1, Cout2, HF0, HF1, HF2, HF3, HF4, HF5, HF6, HF7, HF8, P0, P1, P2, SP0;

  // And and_1 has open pins: In_1=B[7], In_2=A[7], out=open
  // And and_2 has open pins: In_1=B[6], In_2=A[7], out=open
  // And and_3 has open pins: In_1=B[7], In_2=A[6], out=open
  // And and_4 has open pins: In_1=B[6], In_2=A[6], out=open
  // And and_5 has open pins: In_1=B[7], In_2=A[5], out=open
  // And and_6 has open pins: In_1=B[5], In_2=A[7], out=open
  // And and_7 has open pins: In_1=B[4], In_2=A[7], out=open
  // And and_8 has open pins: In_1=B[5], In_2=A[6], out=open
  // And and_9 has open pins: In_1=B[6], In_2=A[5], out=open
  // And and_10 has open pins: In_1=B[7], In_2=A[4], out=open
  // And and_11 has open pins: In_1=B[3], In_2=A[7], out=open
  // And and_12 has open pins: In_1=B[4], In_2=A[6], out=open
  // And and_13 has open pins: In_1=B[5], In_2=A[5], out=open
  // And and_14 has open pins: In_1=B[6], In_2=A[4], out=open
  // And and_15 has open pins: In_1=B[7], In_2=A[3], out=open
  // And and_16 has open pins: In_1=B[2], In_2=A[7], out=open
  // And and_17 has open pins: In_1=B[3], In_2=A[6], out=open
  // And and_18 has open pins: In_1=B[4], In_2=A[5], out=open
  // And and_19 has open pins: In_1=B[5], In_2=A[4], out=open
  // And and_20 has open pins: In_1=B[6], In_2=A[3], out=open
  // And and_21 has open pins: In_1=B[7], In_2=A[2], out=open
  // And and_22 has open pins: In_1=B[6], In_2=A[2], out=open
  // And and_23 has open pins: In_1=B[7], In_2=A[1], out=open
  // And and_24 has open pins: In_1=B[1], In_2=A[7], out=open
  // And and_25 has open pins: In_1=B[2], In_2=A[6], out=open
  // And and_26 has open pins: In_1=B[3], In_2=A[5], out=open
  // And and_27 has open pins: In_1=B[4], In_2=A[4], out=open
  // And and_28 has open pins: In_1=B[5], In_2=A[3], out=open
  // And and_29 has open pins: In_1=B[0], In_2=A[7], out=open
  // And and_30 has open pins: In_1=B[1], In_2=A[6], out=open
  // And and_31 has open pins: In_1=B[2], In_2=A[5], out=open
  // And and_32 has open pins: In_1=B[3], In_2=A[4], out=open
  // And and_33 has open pins: In_1=B[4], In_2=A[3], out=open
  // And and_34 has open pins: In_1=B[5], In_2=A[2], out=open
  // And and_35 has open pins: In_1=B[6], In_2=A[1], out=open
  // And and_36 has open pins: In_1=B[7], In_2=A[0], out=open
  // And and_37 has open pins: In_1=B[0], In_2=A[6], out=open
  // And and_38 has open pins: In_1=B[1], In_2=A[5], out=open
  // And and_39 has open pins: In_1=B[2], In_2=A[4], out=open
  // And and_40 has open pins: In_1=B[3], In_2=A[3], out=open
  // And and_41 has open pins: In_1=B[4], In_2=A[2], out=open
  // And and_42 has open pins: In_1=B[5], In_2=A[1], out=open
  // And and_43 has open pins: In_1=B[6], In_2=A[0], out=open
  // And and_44 has open pins: In_1=B[0], In_2=A[5], out=open
  // And and_45 has open pins: In_1=B[1], In_2=A[4], out=open
  // And and_46 has open pins: In_1=B[2], In_2=A[3], out=open
  // And and_47 has open pins: In_1=B[3], In_2=A[2], out=open
  // And and_48 has open pins: In_1=B[4], In_2=A[1], out=open
  // And and_49 has open pins: In_1=B[5], In_2=A[0], out=open
  // And and_50 has open pins: In_1=B[0], In_2=A[4], out=open
  // And and_51 has open pins: In_1=B[1], In_2=A[3], out=open
  // And and_52 has open pins: In_1=B[2], In_2=A[2], out=open
  // And and_53 has open pins: In_1=B[3], In_2=A[1], out=open
  // And and_54 has open pins: In_1=B[4], In_2=A[0], out=open
  and and_55 (HF5, B[0], A[3]);
  and and_56 (HF6, B[1], A[2]);
  and and_57 (HF7, B[2], A[1]);
  and and_58 (HF8, B[3], A[0]);
  and and_59 (HF2, B[0], A[2]);
  and and_60 (HF3, B[1], A[1]);
  and and_61 (HF4, B[2], A[0]);
  and and_62 (HF0, B[0], A[1]);
  and and_63 (HF1, B[1], A[0]);
  and and_64 (P0, B[0], A[0]);
  soma1bit HF0_plus_HF1 (.A(HF0), .B(HF1), .Cin(1'b0), .S(P1), .Cout(Cout0));
  soma1bit HF2_plus_HF3 (.A(HF2), .B(HF3), .Cin(Cout0), .S(SP0), .Cout(Cout1));
  soma1bit SP0_plus_HF4 (.A(SP0), .B(HF4), .Cin(1'b0), .S(P2), .Cout(Cout2));
endmodule
